// Digital circuit main.dig as structural Verilog
module main (
  input  clk,
  input  reset,
  output [23:0] pc_out,
  output [31:0] mem_din,
  output [31:0] ir_bus,
  output [21:0] ir_offset,
  output [21:0] ir_addr,
  output [5:0] ir_addr_w,
  output [5:0] ir_addr_b,
  output [2:0] wb_sel,
  output [9:0] ir_opcode,
  output [7:0] ctrl_alu_op,
  output [31:0] alu_out,
  output [31:0] reg_w_data,
  output [31:0] p,
  output [15:0] term_data,
  output [15:0] vram_addr,
  output term_we,
  output [23:0] pc_save,
  output [31:0] m_out,
  output [23:0] mem_addr,
  output [2:0] ctrl_w_sel,
  output [31:0] reg_b,
  output [31:0] reg_a,
  output ctrl_reg_we,
  output [5:0] ir_addr_a,
  output [3:0] ir_sel
);

  wire alu_cout, alu_nout, alu_nzout, alu_vout, alu_zout, and_1_out, bank_en, comparator_1_eq,
       comparator_2_eq, ctrl_branch_en, ctrl_bus_sel, ctrl_byte_sel, ctrl_cin_sel, ctrl_cycles,
       ctrl_flags_we, ctrl_jump_type, ctrl_mem_rd, ctrl_mem_wr, ctrl_pc_link_WE, ctrl_pc_src, ctrl_sp_out,
       flag_c, flag_n, flag_v, flag_z, HALT_IN, is_mmio, mem_rd_out, ram_cs, seq_exec, seq_fetch, sp_out,
       vram_we;
  wire [1:0] c_addr_msb2, ctrl_mem_sel, ctrl_shift_op;
  wire [2:0] cond;
  wire [3:0] BANK_SEL;
  wire [4:0] ctrl_alu_pre;
  wire [15:0] vram_data;
  wire [23:0] CPU_ADDR_OUT, mmio_addr;
  wire [31:0] io_data_in, mem_in, mul_out, reg_c, shift_out;

  // program_counter program_counter_1: pin names not known; wires that end beside it: mem_din, alu_out, ctrl_pc_src, ir_offset, reset, ctrl_cycles, clk, flag_n, flag_c, flag_z, flag_v, cond, ctrl_jump_type, ctrl_branch_en, 1'b0, HALT_IN, 1'b0, 1'b0, 1'b0, 1'b0, ctrl_pc_link_WE, pc_out, pc_save, seq_fetch, seq_exec
  register register_1 (
    .WE(ctrl_reg_we), .DATA_W(reg_w_data), .ADDR_A(ir_addr_a), .ADDR_B(ir_addr_b), .ADDR_W(ir_addr_w),
    .EXEC(seq_exec), .clk(clk), .BANK_SEL(BANK_SEL), .Bank_en(bank_en), .DATA_A(reg_a), .DATA_B(reg_b),
    .DATA_C(reg_c));
  store_mux store_mux_1 (
    .reg_a(reg_a), .alu_out(alu_out), .pc_save(pc_save), .reg_b(reg_b), .mem_sel(ctrl_mem_sel),
    .mem_mux(mem_in));
  ir ir_1 (
    .DATA_IN(mem_din), .LOAD(seq_fetch), .CLK(clk), .ir_sel(ir_sel), .RegB(reg_b), .OPCODE(ir_opcode),
    .ADDR_A(ir_addr_a), .ADDR_B(ir_addr_b), .ADDR_W(ir_addr_w), .ADDR_ABS(ir_addr), .OFFSET(ir_offset),
    .COND(cond), .ir_imm_out(ir_bus), .BANK_SEL(BANK_SEL));  // open: MUX1_SEL, MUX2_SEL
  // bus_arbitration bus_arbitration_1: pin names not known; wires that end beside it: seq_fetch, ir_addr, ctrl_mem_rd, ctrl_bus_sel, reg_b, pc_out, sp_out, alu_out, mem_addr, mem_rd_out
  io_controller io_controller_1 (
    .mem_addr(mmio_addr), .c_wr(ctrl_mem_wr), .kb_data(16'h1), .mem_data_out(mem_in),
    .io_data_in(io_data_in), .ram_cs(ram_cs), .vram_we(vram_we), .vram_addr(vram_addr),
    .vram_data(vram_data), .term_we(term_we), .term_data(term_data));
  EEPROMDualPort #(.AddrBits(24), .Bits(32)) eepromdualport_1 (
    .A(CPU_ADDR_OUT), .Din(mem_in), .str(ctrl_mem_wr), .C(clk), .ld(mem_rd_out), .D(m_out));
  // microcode microcode_1: pin names not known; wires that end beside it: ir_opcode, ctrl_alu_op, ctrl_alu_pre, ctrl_cin_sel, ctrl_shift_op, ir_sel, bank_en, ctrl_w_sel, ctrl_reg_we, ctrl_flags_we, ctrl_mem_rd, ctrl_mem_wr, ctrl_byte_sel, ctrl_branch_en, ctrl_jump_type, ctrl_pc_src, ctrl_sp_out, ctrl_cycles, ctrl_bus_sel, ctrl_pc_link_WE, ctrl_mem_sel
  mmio_bus mmio_bus_1 (
    .ADDR(mem_addr), .CPU_ADDR_OUT(CPU_ADDR_OUT), .mmio_addr(mmio_addr), .is_mmio(is_mmio),
    .cpu_addr_msb2(c_addr_msb2));
  Comparator #(.Bits(6)) comparator_1 (.a(6'b000010), .b(ir_addr_w), .eq(comparator_1_eq));  // open: gt, lt
  // mul_div mul_div_1: pin names not known; wires that end beside it: reg_a, ir_bus, mul_out
  // byte_lane_decoder byte_lane_decoder_1: pin names not known; wires that end beside it: m_out, ctrl_byte_sel, io_data_in, c_addr_msb2, mem_din
  and and_1 (and_1_out, seq_exec, ctrl_reg_we, comparator_1_eq);
  shift shift_1 (.A(reg_a), .mode(ctrl_shift_op), .B(ir_bus), .Out(shift_out));
  alu_32b_final alu_32b_final_1 (
    .A(reg_a), .nz0(1'b0), .B(ir_bus), .Opcode(ctrl_alu_op), .control(ctrl_alu_pre), .REG_C(reg_c),
    .cin_sel(ctrl_cin_sel), .FLAG_C(flag_c), .vout(alu_vout), .zout(alu_zout), .nzout(alu_nzout),
    .nout(alu_nout), .Out(alu_out), .cout(alu_cout));
  flag_reg flag_reg_1 (
    .ZERO_IN(alu_zout), .CARRY_IN(alu_cout), .NEGATIVE_IN(alu_nout), .OVERFLOW_IN(alu_vout),
    .FLAG_WE(ctrl_flags_we), .CLK(clk), .EXEC(seq_exec), .FLAG_Z(flag_z), .FLAG_C(flag_c), .FLAG_N(flag_n),
    .FLAG_O(flag_v));
  wb_mux wb_mux_1 (
    .wb_sel(ctrl_w_sel), .alu_out(alu_out), .shift_out(shift_out), .pc_save(pc_save), .mem_din(io_data_in),
    .io_datain(reg_a), .reg_a(ir_bus), .ir_bus(mul_out), .reg_w_data(reg_w_data));
  // sp sp_1: pin names not known; wires that end beside it: mem_din, ctrl_sp_out, clk, reset, alu_out, seq_exec, sp_out
  Register #(.Bits(32)) register_2 (.D(reg_w_data), .C(clk), .en(and_1_out), .Q(p));
  and and_2 (HALT_IN, comparator_2_eq, seq_exec);
  Comparator #(.Bits(10)) comparator_2 (.a(10'hff), .b(ir_opcode), .eq(comparator_2_eq));  // open: gt, lt

  assign wb_sel = ctrl_w_sel;

  // Other names for the same wires on the sheet: ctrl_wb_sel[2:0] = ctrl_w_sel; mem_ram_out[31:0] = m_out

  // Notes on the sheet:
  //   contents of eepromdualport_1 (hex, n*v repeats v):
  //   04001010,0d400420,00000000,00000000,00000042
endmodule

/* Test case memory-test:
reset clk pc-out ir-opcode ctrl-reg-we ctrl-w-sel mem-addr reg-b m-out reg-w-data

# hold (main reset=1) — sync sequencer while held
1 0 x x x x x x x x
1 1 x x x x x x x x
1 0 x x x x x x x x
1 1 x x x x x x x x
# run (main reset=0) — release with clk low, then first edge
0 0 x x x x x x x x
0 0 x x x x x x x x
0 1 x x x x x x x x
# FETCH ADDI @ PC=0
0 0 x x x x x x x x
0 1 x x x x x x x x
# EXECUTE ADDI R1=4 (pc-out=1 on clk=1)
0 1 1 0x10 1 0 x x x 4
0 0 x x x x x x x x
0 1 x x x x x x x x
# FETCH LW0 @ PC=1
0 0 x x x x x x x x
0 1 x x x x x x x x
# EXECUTE LW0 — load 0x42 from mem[4] into R2 (pc-out=2, sample clk=0)
0 0 2 0x35 1 3 4 4 0x42 0x42
*/
